# Fritzing sketch fz-design (saved by Fritzing 0.9.3b)
breadboards: 2

parts:
  M1 = DOIT Esp32 DevKit v1 (30 pins long, 11 pins width) [part_number=ESP32S-PIN30]
  LED1 = smd LED [color="Red (633nm)" package="0805 [SMD]"]
  M2 = DOIT Esp32 DevKit v1 (30 pins long, 11 pins width) [part_number=ESP32S-PIN30]
  LED2 = smd LED [color="Red (633nm)" package="0805 [SMD]"]
  S2 = Pushbutton [package="[THT]"]
  R1 = Resistor [tolerance=±5% resistance=330 package=THT]
  R3 = Resistor [tolerance=±5% resistance=330 package=THT]
  R4 = Resistor [tolerance=±5% resistance=10k package=THT]

nets:
  N1: M1.GND, LED1.cathode
  N2: M1.D32, R1.Pin_1
  N3: LED1.anode, R1.Pin_0
  N4: M2.3V3, S2.Pin_3, S2.Pin_4
  N5: M2.GND, LED2.cathode, R4.Pin_0
  N6: M2.D34, S2.Pin_1, S2.Pin_2, R4.Pin_1
  N7: M2.D32, R3.Pin_1
  N8: LED2.anode, R3.Pin_0

custom parts:
  DOIT Esp32 DevKit v1 (30 pins long, 11 pins width): The DOIT Esp32 DevKit v1 is one of the development board created by DOIT to evaluate the ESP-WROOM-32 module. It is based on the ESP32 microcontroller that boasts Wifi, Bluetooth, Ethernet and Low Power support all in a single chip. (vanepp) made breadboard work, adjusted pin numbering and labels and reduced size of schematic and cleaned up pcb. This chip is 30pins long (2 x15) and 11 pins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
